// Logisim project maman12-q1.circ as structural Verilog: 1 circuit, main circuit main
module main (
  input  a7,
  input  a6,
  input  a5,
  input  a4,
  input  a3,
  input  a2,
  input  a1,
  input  a0,
  input  d,
  output s7,
  output s6,
  output s5,
  output s4,
  output s3,
  output s2,
  output s1,
  output s0
);

  wire and_1_out, and_3_out, and_4_out, and_5_out, and_6_out, and_7_out, and_8_out, and_9_out, and_10_out,
       and_11_out, and_12_out, and_14_out, not_1_out;

  not not_1 (not_1_out, d);
  and and_1 (and_1_out, a7, not_1_out);
  and and_2 (s7, d, a6);
  and and_3 (and_3_out, a6, not_1_out);
  and and_4 (and_4_out, d, a5);
  and and_5 (and_5_out, a5, not_1_out);
  and and_6 (and_6_out, d, a4);
  and and_7 (and_7_out, a4, not_1_out);
  and and_8 (and_8_out, a3, d);
  and and_9 (and_9_out, a3, not_1_out);
  and and_10 (and_10_out, a2, d);
  and and_11 (and_11_out, a2, not_1_out);
  and and_12 (and_12_out, a1, d);
  and and_13 (s0, a1, not_1_out);
  and and_14 (and_14_out, d, a0);
  or or_1 (s6, and_1_out, and_4_out);
  or or_2 (s5, and_3_out, and_6_out);
  or or_3 (s4, and_5_out, and_8_out);
  or or_4 (s3, and_7_out, and_10_out);
  or or_5 (s2, and_9_out, and_12_out);
  or or_6 (s1, and_11_out, and_14_out);
endmodule
